# Fritzing sketch t-sonde-breadboard-fritzing (saved by Fritzing 1.0.5)
breadboards: 1

parts:
  Wifi_Kit_8 = Heltec WiFi Kit 8 [part_number=HTIT-W8266]
  R1 = Resistor [tolerance=±5% power=0.25W resistance=4.7k package=THT]
  DS1 = DS18B20 1-Wire Temperature Sensor [part_number=DS18B20]

nets:
  N1: Wifi_Kit_8.pin_6, R1.Pin_1, DS1.DQ
  N2: Wifi_Kit_8.pin_10, R1.Pin_0, DS1.VDD
  N3: Wifi_Kit_8.pin_12, DS1.GND
  N4: Wifi_Kit_8.pin_15, Wifi_Kit_8.pin_18, Wifi_Kit_8.pin_19
  N5: Wifi_Kit_8.pin_16, Wifi_Kit_8.pin_21
  N6: Wifi_Kit_8.pin_17, Wifi_Kit_8.pin_20

custom parts:
  Heltec WiFi Kit 8: The Heltec WiFi Kit 8 is an IoT development board designed and produced by Heltec Automation and based on the Espressif ESP8266 processor module. The board includes built-in WiFi, a 0.91″ OLED display and a Li-Po battery management system. Links: Heltec WiFi Kit 32 product page Github
